# Fritzing sketch seven-segment_display_rps (saved by Fritzing 0.9.0b)
breadboards: 1

parts:
  Intel(R)_Galileo_1 = Intel(R) Galileo
  7_Segment2 = 7 Segment Display
  R3 = Resistor [tolerance=±5% resistance=330 package=THT]
  7_Segment3 = 7 Segment Display
  R4 = Resistor [tolerance=±5% resistance=330 package=THT]
  S1 = Pushbutton [package="[THT]"]
  S2 = Pushbutton [package="[THT]"]
  S3 = Pushbutton [package="[THT]"]
  S4 = Pushbutton [package="[THT]"]
  S5 = Pushbutton [package="[THT]"]
  S6 = Pushbutton [package="[THT]"]
  R5 = Resistor [tolerance=±5% resistance=10k package=THT]
  R6 = Resistor [tolerance=±5% resistance=10k package=THT]
  R7 = Resistor [tolerance=±5% resistance=10k package=THT]
  R8 = Resistor [tolerance=±5% resistance=10k package=THT]
  R9 = Resistor [tolerance=±5% resistance=10k package=THT]
  R10 = Resistor [tolerance=±5% resistance=10k package=THT]

nets:
  N1: Intel(R)_Galileo_1.A0, S1.Pin_1, S1.Pin_2, R8.Pin_1
  N2: Intel(R)_Galileo_1.A1, S2.Pin_1, S2.Pin_2, R10.Pin_1
  N3: Intel(R)_Galileo_1.A2, S3.Pin_1, S3.Pin_2, R9.Pin_1
  N4: Intel(R)_Galileo_1.A3, S4.Pin_1, S4.Pin_2, R5.Pin_1
  N5: Intel(R)_Galileo_1.A4/SDA, S5.Pin_1, S5.Pin_2, R6.Pin_1
  N6: Intel(R)_Galileo_1.A5/SCL, S6.Pin_1, S6.Pin_2, R7.Pin_1
  N7: Intel(R)_Galileo_1.D8, 7_Segment3.common_cathode, R4.Pin_1
  N8: Intel(R)_Galileo_1.D9_PWM, 7_Segment3.Segment_G
  N9: Intel(R)_Galileo_1.D10_PWM/SS, 7_Segment3.Segment_D
  N10: Intel(R)_Galileo_1.D11_PWM/MOSI, 7_Segment3.Segment_F
  N11: Intel(R)_Galileo_1.D12/MISO, 7_Segment3.Segment_A
  N12: Intel(R)_Galileo_1.D13/SCK, 7_Segment3.Segment_B
  N13: Intel(R)_Galileo_1.D0/RX, 7_Segment2.Segment_C
  N14: Intel(R)_Galileo_1.D1/TX, 7_Segment2.Segment_D
  N15: Intel(R)_Galileo_1.D2, 7_Segment2.Segment_G
  N16: Intel(R)_Galileo_1.D3_PWM, 7_Segment2.Segment_E
  N17: Intel(R)_Galileo_1.D4, 7_Segment2.Segment_F
  N18: Intel(R)_Galileo_1.D5_PWM, 7_Segment2.Segment_A
  N19: Intel(R)_Galileo_1.D6_PWM, 7_Segment2.Segment_B
  N20: Intel(R)_Galileo_1.D7, 7_Segment3.Segment_C
  N21: Intel(R)_Galileo_1.5V, R3.Pin_0, R4.Pin_0, R5.Pin_0, R6.Pin_0, R7.Pin_0, R8.Pin_0, R9.Pin_0, R10.Pin_0
  N22: 7_Segment2.common_cathode, R3.Pin_1
  N23: S1.Pin_3, S1.Pin_4
  N24: S2.Pin_3, S2.Pin_4
  N25: S3.Pin_3, S3.Pin_4
  N26: S4.Pin_3, S4.Pin_4
  N27: S5.Pin_3, S5.Pin_4
  N28: S6.Pin_3, S6.Pin_4

custom parts:
  Intel(R) Galileo: Galileo is a microcontroller board based on the Intel® Quark SoC X1000 Application Processor, a 32-bit Intel Pentium-class system on a chip (datasheet). It’s the first board based on Intel® architecture designed to be hardware and software pin-compatible with Arduino shields designed for the Uno R3. Digital pins 0 to 13 (and the adjacent AREF and GND pins), Analog inputs 0 to 5, the power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
