# Fritzing sketch seven-segment_display_rps_single (saved by Fritzing 0.9.0b)
breadboards: 1

parts:
  Intel(R)_Galileo_1 = Intel(R) Galileo
  7_Segment2 = 7 Segment Display
  R3 = Resistor [tolerance=±5% resistance=330 package=THT]
  S4 = Pushbutton [package="[THT]"]
  S5 = Pushbutton [package="[THT]"]
  S6 = Pushbutton [package="[THT]"]
  R5 = Resistor [tolerance=±5% resistance=10k package=THT]
  R6 = Resistor [tolerance=±5% resistance=10k package=THT]
  R7 = Resistor [tolerance=±5% resistance=10k package=THT]

nets:
  N1: Intel(R)_Galileo_1.A3, S4.Pin_1, S4.Pin_2, R5.Pin_1
  N2: Intel(R)_Galileo_1.A4/SDA, S5.Pin_1, S5.Pin_2, R6.Pin_1
  N3: Intel(R)_Galileo_1.A5/SCL, S6.Pin_1, S6.Pin_2, R7.Pin_1
  N4: Intel(R)_Galileo_1.D0/RX, 7_Segment2.Segment_C
  N5: Intel(R)_Galileo_1.D1/TX, 7_Segment2.Segment_D
  N6: Intel(R)_Galileo_1.D2, 7_Segment2.Segment_E
  N7: Intel(R)_Galileo_1.D3_PWM, 7_Segment2.Segment_F
  N8: Intel(R)_Galileo_1.D4, 7_Segment2.Segment_G
  N9: Intel(R)_Galileo_1.D5_PWM, 7_Segment2.Segment_A
  N10: Intel(R)_Galileo_1.D6_PWM, 7_Segment2.Segment_B
  N11: Intel(R)_Galileo_1.5V, R3.Pin_0, R5.Pin_0, R6.Pin_0, R7.Pin_0
  N12: 7_Segment2.common_cathode, R3.Pin_1
  N13: S4.Pin_3, S4.Pin_4
  N14: S5.Pin_3, S5.Pin_4
  N15: S6.Pin_3, S6.Pin_4

custom parts:
  Intel(R) Galileo: Galileo is a microcontroller board based on the Intel® Quark SoC X1000 Application Processor, a 32-bit Intel Pentium-class system on a chip (datasheet). It’s the first board based on Intel® architecture designed to be hardware and software pin-compatible with Arduino shields designed for the Uno R3. Digital pins 0 to 13 (and the adjacent AREF and GND pins), Analog inputs 0 to 5, the power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
